# Fritzing sketch dock_board_twin3_i2c (saved by Fritzing 0.8.3b)
circuit board: 3.04761cm x 4.99626cm
stripboards: 1

parts:
  SLOT0 = female pin header, 5 pins [form="♀ (female)"]
  SLOT1 = female pin header, 5 pins [form="♀ (female)"]
  SLOT2 = female pin header, 5 pins [form="♀ (female)"]
  J1 = male pin header, 7 pins [form="♂ (male)"]
  J2 = male pin header, 4 pins [form="♂ (male)"]

nets:
  GND: SLOT0.pin1, SLOT1.pin1, SLOT2.pin1, J1.pin1, J2.pin4
  N1: SLOT0.pin2, SLOT1.pin2, SLOT2.pin2, J1.pin2, J2.pin3
  N2: SLOT0.pin3, J1.pin7
  N3: SLOT0.pin4, SLOT1.pin4, SLOT2.pin4, J1.pin3, J2.pin2
  N4: SLOT0.pin5, SLOT1.pin5, SLOT2.pin5, J1.pin4, J2.pin1
  N5: SLOT1.pin3, J1.pin6
  N6: SLOT2.pin3, J1.pin5

notes:
  Clixx.IO, Three Port TwinTab Dock, 1B
  P01 - GND
  P02 - VCC
  P03 - SDA
  P04 - SCL
  P05 - Slot 2 Extra
  P06 - Slot 1 Extra
  P07 - Slot 0 Extra
  http://thegaragelab.com
