# Fritzing sketch dock_board_twin3_spi (saved by Fritzing 0.8.3b)
circuit board: 3.04761cm x 4.99626cm
stripboards: 1

parts:
  SLOT0 = female pin header, 5 pins [form="♀ (female)"]
  SLOT1 = female pin header, 5 pins [form="♀ (female)"]
  SLOT2 = female pin header, 5 pins [form="♀ (female)"]
  S0_X = female pin header, 2 pins [form="♀ (female)"]
  S1_X = female pin header, 2 pins [form="♀ (female)"]
  S2_X = female pin header, 2 pins [form="♀ (female)"]
  J1 = male pin header, 11 pins [form="♂ (male)"]

nets:
  GND: SLOT0.pin1, SLOT1.pin1, SLOT2.pin1, J1.pin1
  N1: SLOT0.pin2, SLOT1.pin2, SLOT2.pin2, J1.pin2
  N2: SLOT0.pin3, SLOT1.pin3, SLOT2.pin3, J1.pin3
  N3: SLOT0.pin4, SLOT1.pin4, SLOT2.pin4, J1.pin4
  N4: SLOT0.pin5, SLOT1.pin5, SLOT2.pin5, J1.pin5
  N5: S0_X.pin1, J1.pin6
  N6: S0_X.pin2, J1.pin7
  N7: S1_X.pin1, J1.pin8
  N8: S1_X.pin2, J1.pin9
  N9: S2_X.pin1, J1.pin10
  N10: S2_X.pin2, J1.pin11

notes:
  Clixx.IO, Three Port TwinTab Dock, 1B
  P01 - GND
  P02 - VCC
  P03 - SDA
  P04 - SCL
  P05 - Slot 2 Extra
  P06 - Slot 1 Extra
  P07 - Slot 0 Extra
  http://thegaragelab.com
