# Fritzing sketch dock_board_twin6 (saved by Fritzing 0.8.3b)
circuit board: 5.34cm x 5cm
stripboards: 1

parts:
  J1 = male pin header, 20 pins [form="♂ (male)"]
  SLOT0 = female pin header, 5 pins [form="♀ (female)"]
  SLOT1 = female pin header, 5 pins [form="♀ (female)"]
  SLOT2 = female pin header, 5 pins [form="♀ (female)"]
  SLOT3 = female pin header, 5 pins [form="♀ (female)"]
  SLOT4 = female pin header, 5 pins [form="♀ (female)"]
  SLOT5 = female pin header, 5 pins [form="♀ (female)"]

nets:
  N1: J1.pin1, SLOT0.pin1, SLOT1.pin1, SLOT2.pin1, SLOT3.pin1, SLOT4.pin1, SLOT5.pin1
  N2: J1.pin2, SLOT0.pin2, SLOT1.pin2, SLOT2.pin2, SLOT3.pin2, SLOT4.pin2, SLOT5.pin2
  N3: J1.pin3, SLOT0.pin3
  N4: J1.pin4, SLOT0.pin4
  N5: J1.pin5, SLOT0.pin5
  N6: J1.pin6, SLOT1.pin3
  N7: J1.pin7, SLOT1.pin4
  N8: J1.pin8, SLOT1.pin5
  N9: J1.pin9, SLOT2.pin3
  N10: J1.pin10, SLOT2.pin4
  N11: J1.pin11, SLOT2.pin5
  N12: J1.pin12, SLOT3.pin3
  N13: J1.pin13, SLOT3.pin4
  N14: J1.pin14, SLOT3.pin5
  N15: J1.pin15, SLOT4.pin3
  N16: J1.pin16, SLOT4.pin4
  N17: J1.pin17, SLOT4.pin5
  N18: J1.pin18, SLOT5.pin3
  N19: J1.pin19, SLOT5.pin4
  N20: J1.pin20, SLOT5.pin5

notes:
  Clixx.IO, Six Port TwinTab Dock, 1A
  P01 - GND
  P02 - VCC
  P03 - Slot 0 Extra
  P04 - Slot 0 In
  P05 - Slot 0 Out
  P06 - Slot 1 Extra
  P07 - Slot 1 In
  P08 - Slot 1 Out
  P09 - Slot 2 Extra
  P10 - Slot 2 In
  P11 - Slot 2 Out
  P16 - Slot 4 In
  P17 - Slot 4 Out
  P13 - Slot 3 In
  P15 - Slot 4 Extra
  P14 - Slot 3 Out
  P20 - Slot 5 Out
  P18 - Slot 5 Extra
  P19 - Slot 5 In
  P12 - Slot 3 Extra
